// Logisim project Controller.circ as structural Verilog: 1 circuit, main circuit Control Store
module Control_Store (
  input  [7:0] Instruction,
  input  [3:0] in_2,
  output out_3,
  output out_4,
  output out_5,
  output out_6,
  output out_7,
  output out_8
);

  wire and_1_out, and_2_out, and_3_out, and_4_out, and_5_out, and_6_out, and_7_out, and_8_out, and_9_out,
       and_10_out, and_11_out, not_1_out, not_2_out, not_3_out, not_4_out;

  not not_1 (not_1_out, in_2[3]);
  not not_2 (not_2_out, in_2[2]);
  not not_3 (not_3_out, in_2[1]);
  not not_4 (not_4_out, in_2[0]);
  and and_1 (and_1_out, not_1_out, not_2_out);
  and and_2 (and_2_out, not_2_out, in_2[0]);
  or or_1 (out_3, and_1_out, and_2_out, and_3_out);
  and and_3 (and_3_out, in_2[1], not_4_out);
  or or_2 (out_4, not_2_out, in_2[1], in_2[0]);
  or or_3 (out_5, in_2[3], in_2[2], in_2[1], not_4_out);
  and and_4 (and_4_out, not_1_out, not_3_out, in_2[0]);
  and and_5 (and_5_out, in_2[2], not_3_out);
  or or_4 (out_6, and_4_out, and_5_out, and_6_out);
  and and_6 (and_6_out, not_2_out, in_2[1]);
  and and_7 (and_7_out, not_2_out, in_2[0]);
  or or_5 (out_7, and_7_out, and_8_out);
  and and_8 (and_8_out, in_2[3], not_2_out, not_3_out);
  and and_9 (and_9_out, not_1_out, not_2_out, in_2[1], not_4_out);
  and and_10 (and_10_out, not_2_out, in_2[1], in_2[0]);
  or or_6 (out_8, and_9_out, and_10_out, and_11_out);
  and and_11 (and_11_out, in_2[3], not_2_out, in_2[0]);

  // Notes on the sheet:
  //   A
  //   B
  //   C
  //   D
  //   F0
  //   F1
  //   ENA
  //   ENB
  //   INVA
  //   INC
endmodule
